// Logisim project Lab2.circ as structural Verilog: 7 circuits, main circuit main
module main (
);


  // Notes on the sheet:
  //   Lab 2
  //   PI Name
  //   Your Name
endmodule

module mux_2x1 (
  input  S,
  input  A,
  input  B,
  output C
);

  // NOT_Gate not_1 has open pins: in=S, out=open
  // NOT_Gate not_2 has open pins: in=A, out=open
  // NOT_Gate not_3 has open pins: in=B, out=open
endmodule

module mux_4x1 (
  input  S1,
  input  S0,
  input  A,
  input  B,
  input  C,
  input  D,
  output E
);
endmodule

module part3a (
  input  B1,
  input  B0,
  output A,
  output B,
  output C,
  output D,
  output E,
  output F,
  output G
);


  // Notes on the sheet:
  //   part3a
endmodule

module seven_segment (
  input  B0,
  input  B1,
  input  B2,
  input  B3,
  output [7:0] display_out
);
endmodule

module mux_4x1_8bit (
  input  S1,
  input  S0,
  input  [7:0] A,
  input  [7:0] B,
  input  [7:0] C,
  input  [7:0] D,
  output [7:0] E
);

  mux_4x1 mux_0 (.S1(S1), .S0(S0), .A(A[0]), .B(B[0]), .C(C[0]), .D(D[0]), .E(E[0]));
  mux_4x1 mux_1 (.S1(S1), .S0(S0), .A(A[1]), .B(B[1]), .C(C[1]), .D(D[1]), .E(E[1]));
  mux_4x1 mux_2 (.S1(S1), .S0(S0), .A(A[2]), .B(B[2]), .C(C[2]), .D(D[2]), .E(E[2]));
  mux_4x1 mux_3 (.S1(S1), .S0(S0), .A(A[3]), .B(B[3]), .C(C[3]), .D(D[3]), .E(E[3]));
  mux_4x1 mux_4 (.S1(S1), .S0(S0), .A(A[4]), .B(B[4]), .C(C[4]), .D(D[4]), .E(E[4]));
  mux_4x1 mux_5 (.S1(S1), .S0(S0), .A(A[5]), .B(B[5]), .C(C[5]), .D(D[5]), .E(E[5]));
  mux_4x1 mux_6 (.S1(S1), .S0(S0), .A(A[6]), .B(B[6]), .C(C[6]), .D(D[6]), .E(E[6]));
  mux_4x1 mux_7 (.S1(S1), .S0(S0), .A(A[7]), .B(B[7]), .C(C[7]), .D(D[7]), .E(E[7]));
endmodule

module part4 (
  input  S1,
  input  S0
);
endmodule
